# Fritzing sketch IceWeatherstation (saved by Fritzing 1.0.6)

parts:
  ESP32-WROOM-32U_DevKitC_V4 = ESP32 DevKitc V4
  BME280_(Temp/Feuchte/Druck) = BME280 Breakout
  AS3935_Blitzsensor_(CJMCU-3935)_--_Platzhalter-Footprint_(MPU6050/GY-521-Form_kein_exaktes_Fritzing-Part_verfuegbar) = InvenSense MPU6050
  DS18B20_(wasserdichte_Zusatz-Temp-Sonde) = DS18B20 1-Wire Temperature Sensor
  SEN0232_dBA-Sensor_--_Platzhalter-Footprint_(TEMT6000-Form_analog_VCC/GND/S_passt_exakt) = Ambient Light Sensor (TEMT6000 Breakout Board)
  SSD1306_OLED_0_96"_I2C_--_Platzhalter-Footprint_(Grove-Form_GND/VCC/SDA/SCL_passt_exakt) = Grove OLED 128x96
  Regenmesser_(Reed-Kontakt_SEN-15901) = Reed switch [package=THT]
  Anemometer_(Reed-Kontakt_SEN-15901) = Reed switch [package=THT]
  Windfahne_(Variabler_Widerstand_SEN-15901) = Trimmer Potentiometer [package=THT]
  Status-LED_(LedLink_WLAN/MQTT-Aktivitaet) = Red LED - 5mm [package="5 mm [THT]"]
  R1_330R_(LED-Vorwiderstand) = 220 Ω Resistor [package=THT]
  R2_4_7k_(DS18B20_Pull-up_gegen_3_3V) = 220 Ω Resistor [package=THT]
  R3_10k_(Windfahne_Spannungsteiler_fest_gegen_3_3V) = 220 Ω Resistor [package=THT]

nets:
  VCC: ESP32-WROOM-32U_DevKitC_V4.Pin_1, BME280_(Temp/Feuchte/Druck).3.3V, AS3935_Blitzsensor_(CJMCU-3935)_--_Platzhalter-Footprint_(MPU6050/GY-521-Form_kein_exaktes_Fritzing-Part_verfuegbar).VCC, AS3935_Blitzsensor_(CJMCU-3935)_--_Platzhalter-Footprint_(MPU6050/GY-521-Form_kein_exaktes_Fritzing-Part_verfuegbar).AD0, DS18B20_(wasserdichte_Zusatz-Temp-Sonde).VDD, SEN0232_dBA-Sensor_--_Platzhalter-Footprint_(TEMT6000-Form_analog_VCC/GND/S_passt_exakt).VCC, SSD1306_OLED_0_96"_I2C_--_Platzhalter-Footprint_(Grove-Form_GND/VCC/SDA/SCL_passt_exakt).VCC, R2_4_7k_(DS18B20_Pull-up_gegen_3_3V).Pin_1, R3_10k_(Windfahne_Spannungsteiler_fest_gegen_3_3V).Pin_1
  N1: ESP32-WROOM-32U_DevKitC_V4.Pin_5, Windfahne_(Variabler_Widerstand_SEN-15901).leg2, R3_10k_(Windfahne_Spannungsteiler_fest_gegen_3_3V).Pin_0
  N2: ESP32-WROOM-32U_DevKitC_V4.Pin_6, SEN0232_dBA-Sensor_--_Platzhalter-Footprint_(TEMT6000-Form_analog_VCC/GND/S_passt_exakt).S
  N3: ESP32-WROOM-32U_DevKitC_V4.Pin_9, AS3935_Blitzsensor_(CJMCU-3935)_--_Platzhalter-Footprint_(MPU6050/GY-521-Form_kein_exaktes_Fritzing-Part_verfuegbar).INT
  N4: ESP32-WROOM-32U_DevKitC_V4.Pin_11, Regenmesser_(Reed-Kontakt_SEN-15901).pin_2
  N5: ESP32-WROOM-32U_DevKitC_V4.Pin_12, Anemometer_(Reed-Kontakt_SEN-15901).pin_2
  GND: ESP32-WROOM-32U_DevKitC_V4.Pin_14, ESP32-WROOM-32U_DevKitC_V4.Pin_32, ESP32-WROOM-32U_DevKitC_V4.Pin_38, BME280_(Temp/Feuchte/Druck).GND, AS3935_Blitzsensor_(CJMCU-3935)_--_Platzhalter-Footprint_(MPU6050/GY-521-Form_kein_exaktes_Fritzing-Part_verfuegbar).GND, DS18B20_(wasserdichte_Zusatz-Temp-Sonde).GND, SEN0232_dBA-Sensor_--_Platzhalter-Footprint_(TEMT6000-Form_analog_VCC/GND/S_passt_exakt).GND, SSD1306_OLED_0_96"_I2C_--_Platzhalter-Footprint_(Grove-Form_GND/VCC/SDA/SCL_passt_exakt).GND, Regenmesser_(Reed-Kontakt_SEN-15901).pin_1, Anemometer_(Reed-Kontakt_SEN-15901).pin_1, Windfahne_(Variabler_Widerstand_SEN-15901).leg1, Status-LED_(LedLink_WLAN/MQTT-Aktivitaet).cathode
  N6: ESP32-WROOM-32U_DevKitC_V4.Pin_24, R1_330R_(LED-Vorwiderstand).Pin_1
  N7: ESP32-WROOM-32U_DevKitC_V4.Pin_26, DS18B20_(wasserdichte_Zusatz-Temp-Sonde).DQ, R2_4_7k_(DS18B20_Pull-up_gegen_3_3V).Pin_0
  N8: ESP32-WROOM-32U_DevKitC_V4.Pin_33, BME280_(Temp/Feuchte/Druck).SDI/SDA, AS3935_Blitzsensor_(CJMCU-3935)_--_Platzhalter-Footprint_(MPU6050/GY-521-Form_kein_exaktes_Fritzing-Part_verfuegbar).SDA, SSD1306_OLED_0_96"_I2C_--_Platzhalter-Footprint_(Grove-Form_GND/VCC/SDA/SCL_passt_exakt).SDA
  N9: ESP32-WROOM-32U_DevKitC_V4.Pin_36, BME280_(Temp/Feuchte/Druck).SCK/SCL, AS3935_Blitzsensor_(CJMCU-3935)_--_Platzhalter-Footprint_(MPU6050/GY-521-Form_kein_exaktes_Fritzing-Part_verfuegbar).SCL, SSD1306_OLED_0_96"_I2C_--_Platzhalter-Footprint_(Grove-Form_GND/VCC/SDA/SCL_passt_exakt).SCL
  N10: Status-LED_(LedLink_WLAN/MQTT-Aktivitaet).anode, R1_330R_(LED-Vorwiderstand).Pin_0

custom parts:
  ESP32 DevKitc V4: ESP32-DevKitC board with ESP32-WROOM-32 module. ESP32-DevKitC V4 is a small-sized ESP32-based development board produced by Espressif. Most of the pins on the ESP module are broken out to the pin headers on the board. The pins D0, D1, D2, D3, CMD and CLK are used internally for communication between ESP32 and SPI flash memory. They are grouped on both sides near the USB connector. Avoid using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
